// Logisim project JK FLIP FLOP.circ as structural Verilog: 1 circuit, main circuit main
module main (
  input  in_1,
  input  in_2,
  output out_3,
  output out_4,
  output out_5
);

  wire and_1_out, or_1_out;

  J_K_Flip_Flop #(.trigger("falling")) A (.J(in_1), .clk(in_2), .K(in_1), .Q(out_3));  // open: Qn, preset, en, reset
  or or_1 (or_1_out, out_3, out_5);
  J_K_Flip_Flop #(.trigger("falling")) B (
    .J(out_3), .clk(in_2), .K(or_1_out), .Q(out_4));  // open: Qn, preset, en, reset
  and and_1 (and_1_out, out_3, out_4);
  J_K_Flip_Flop #(.trigger("falling")) C (
    .J(and_1_out), .clk(in_2), .K(out_4), .Q(out_5));  // open: Qn, preset, en, reset
endmodule
