// Logisim project BCD.circ as structural Verilog: 2 circuits, main circuit main
module main (
  input  a,
  input  b,
  input  c,
  input  d,
  output a_2,
  output f,
  output b_2,
  output g,
  output e,
  output c_2,
  output d_2
);

  wire nand_1_out, nand_2_out, nand_3_out, nand_4_out, nand_5_out, nand_6_out, nand_7_out, nand_8_out,
       nand_9_out, nand_10_out, nand_11_out, nand_12_out, nand_13_out, nand_14_out, nand_15_out, nand_16_out,
       nand_17_out, nand_18_out, nand_19_out, nand_20_out, nand_21_out, nand_22_out, nand_23_out,
       nand_24_out, nand_25_out, nand_26_out, nand_27_out, nand_29_out, nand_30_out, nand_31_out,
       nand_32_out, nand_33_out, nand_34_out, nand_35_out, nand_36_out, nand_37_out, nand_38_out,
       nand_39_out, nand_40_out, nand_41_out, nand_42_out, nand_43_out;

  nand nand_1 (nand_1_out, b, b);
  nand nand_2 (nand_2_out, d, d);
  nand nand_3 (nand_3_out, c, c);
  nand nand_4 (nand_4_out, d, d);
  nand nand_5 (nand_5_out, d, d);
  nand nand_6 (nand_6_out, b, b);
  nand nand_7 (nand_7_out, b, b);
  nand nand_8 (nand_8_out, d, d);
  nand nand_9 (nand_9_out, b, b);
  nand nand_10 (nand_10_out, d, d);
  nand nand_11 (nand_11_out, c, c);
  nand nand_12 (nand_12_out, b, b);
  nand nand_13 (nand_13_out, d, d);
  nand nand_14 (nand_14_out, d, d);
  nand nand_15 (nand_15_out, c, c);
  nand nand_16 (nand_16_out, d, d);
  nand nand_17 (nand_17_out, c, c);
  nand nand_18 (nand_18_out, d, d);
  nand nand_19 (nand_19_out, b, b);
  nand nand_20 (nand_20_out, c, c);
  nand nand_21 (nand_21_out, d, d);
  nand nand_22 (nand_22_out, nand_1_out, nand_2_out);
  nand nand_23 (nand_23_out, c, c);
  nand nand_24 (nand_24_out, b, d);
  nand nand_25 (nand_25_out, a, a);
  nand nand_26 (nand_26_out, nand_3_out, nand_4_out);
  nand nand_27 (nand_27_out, c, d);
  nand nand_28 (c_2, c, nand_5_out, nand_6_out);
  nand nand_29 (nand_29_out, nand_7_out, nand_8_out);
  nand nand_30 (nand_30_out, nand_9_out, c);
  nand nand_31 (nand_31_out, c, nand_10_out);
  nand nand_32 (nand_32_out, b, nand_11_out, d);
  nand nand_33 (nand_33_out, a, a);
  nand nand_34 (nand_34_out, nand_12_out, nand_13_out);
  nand nand_35 (nand_35_out, c, nand_14_out);
  nand nand_36 (nand_36_out, nand_15_out, nand_16_out);
  nand nand_37 (nand_37_out, b, nand_17_out);
  nand nand_38 (nand_38_out, b, nand_18_out);
  nand nand_39 (nand_39_out, a, a);
  nand nand_40 (nand_40_out, nand_19_out, c);
  nand nand_41 (nand_41_out, b, nand_20_out);
  nand nand_42 (nand_42_out, b, nand_21_out);
  nand nand_43 (nand_43_out, a, a);
  nand nand_44 (a_2, nand_22_out, nand_23_out, nand_24_out, nand_25_out);
  nand nand_45 (b_2, b, nand_26_out, nand_27_out);
  nand nand_46 (d_2, nand_29_out, nand_30_out, nand_31_out, nand_32_out, nand_33_out);
  nand nand_47 (e, nand_34_out, nand_35_out);
  nand nand_48 (f, nand_36_out, nand_37_out, nand_38_out, nand_39_out);
  nand nand_49 (g, nand_40_out, nand_41_out, nand_42_out, nand_43_out);
endmodule

module \new  (
  input  d,
  input  c,
  input  b,
  input  a,
  output out_5,
  output out_6,
  output out_7,
  output a_2,
  output out_9,
  output out_10,
  output out_11,
  output out_12,
  output out_13,
  output out_14,
  output out_15,
  output out_16,
  output out_17,
  output out_18,
  output out_19,
  output out_20,
  output f,
  output b_2,
  output out_23,
  output out_24,
  output out_25,
  output out_26,
  output out_27,
  output out_28,
  output g,
  output out_30,
  output out_31,
  output out_32,
  output out_33,
  output out_34,
  output out_35,
  output e,
  output out_37,
  output out_38,
  output c_2,
  output out_40,
  output out_41,
  output out_42,
  output out_43,
  output out_44,
  output out_45,
  output out_46,
  output out_47,
  output out_48,
  output d_2,
  output out_50,
  output out_51,
  output out_52,
  output out_53
);

  wire and_1_out, and_2_out, and_3_out, and_4_out, and_5_out, and_6_out, and_7_out, and_8_out, and_9_out,
       and_10_out, and_11_out, and_12_out, and_13_out, and_14_out, and_15_out, and_16_out, not_1_out,
       not_2_out, not_3_out, not_4_out, not_5_out, not_6_out, not_7_out, not_8_out, not_9_out, not_10_out,
       not_11_out, not_12_out, not_13_out, not_14_out, not_15_out, not_16_out, not_17_out, not_18_out,
       not_19_out, not_20_out, not_21_out;

  not not_1 (not_1_out, c);
  and and_1 (and_1_out, not_1_out, not_2_out);
  not not_2 (not_2_out, a);
  and and_2 (and_2_out, c, a);
  not not_3 (not_3_out, c);
  not not_4 (not_4_out, b);
  and and_3 (and_3_out, not_4_out, not_5_out);
  not not_5 (not_5_out, a);
  and and_4 (and_4_out, b, a);
  not not_6 (not_6_out, b);
  or or_1 (c_2, not_6_out, a, c);
  not not_7 (not_7_out, c);
  and and_5 (and_5_out, not_7_out, not_8_out);
  not not_8 (not_8_out, a);
  not not_9 (not_9_out, c);
  and and_6 (and_6_out, not_9_out, b);
  and and_7 (and_7_out, b, not_10_out);
  not not_10 (not_10_out, a);
  not not_11 (not_11_out, b);
  and and_8 (and_8_out, c, not_11_out, a);
  not not_12 (not_12_out, c);
  and and_9 (and_9_out, not_12_out, not_13_out);
  not not_13 (not_13_out, a);
  and and_10 (and_10_out, b, not_14_out);
  not not_14 (not_14_out, a);
  not not_15 (not_15_out, b);
  and and_11 (and_11_out, not_15_out, not_16_out);
  not not_16 (not_16_out, a);
  and and_12 (and_12_out, c, not_17_out);
  not not_17 (not_17_out, b);
  and and_13 (and_13_out, c, not_18_out);
  not not_18 (not_18_out, a);
  not not_19 (not_19_out, c);
  and and_14 (and_14_out, not_19_out, b);
  and and_15 (and_15_out, c, not_20_out);
  not not_20 (not_20_out, b);
  and and_16 (and_16_out, c, not_21_out);
  not not_21 (not_21_out, a);
  or or_2 (a_2, and_1_out, b, and_2_out, d);
  or or_3 (b_2, not_3_out, and_3_out, and_4_out);
  or or_4 (d_2, and_5_out, and_6_out, and_7_out, and_8_out, d);
  or or_5 (e, and_9_out, and_10_out);
  or or_6 (f, and_11_out, and_12_out, and_13_out, d);
  or or_7 (g, and_14_out, and_15_out, and_16_out, d);

  assign out_5 = a_2;
  assign out_6 = a_2;
  assign out_7 = a_2;
  assign out_9 = a_2;
  assign out_10 = a_2;
  assign out_11 = a_2;
  assign out_12 = a_2;
  assign out_13 = f;
  assign out_14 = b_2;
  assign out_15 = f;
  assign out_16 = b_2;
  assign out_17 = f;
  assign out_18 = b_2;
  assign out_19 = f;
  assign out_20 = b_2;
  assign out_23 = f;
  assign out_24 = b_2;
  assign out_25 = g;
  assign out_26 = g;
  assign out_27 = g;
  assign out_28 = g;
  assign out_30 = g;
  assign out_31 = g;
  assign out_32 = g;
  assign out_33 = g;
  assign out_34 = e;
  assign out_35 = c_2;
  assign out_37 = c_2;
  assign out_38 = e;
  assign out_40 = e;
  assign out_41 = c_2;
  assign out_42 = e;
  assign out_43 = c_2;
  assign out_44 = e;
  assign out_45 = c_2;
  assign out_46 = d_2;
  assign out_47 = d_2;
  assign out_48 = d_2;
  assign out_50 = d_2;
  assign out_51 = d_2;
  assign out_52 = d_2;
  assign out_53 = d_2;
endmodule
